# Fritzing sketch Project (saved by Fritzing 0.9.3b)
breadboards: 1

parts:
  Part1 = Arduino Uno (Rev3) - ICSP
  LED1 = smd LED [color="Red (633nm)" package="0805 [SMD]"]
  Part2 = Breakout Board for Electret Microphone
  R1 = Resistor [tolerance=±5% resistance=560 package="0402 [SMD]"]
  LED2 = smd LED [color="Red (633nm)" package="0805 [SMD]"]
  R2 = Resistor [tolerance=±5% resistance=560 package="0402 [SMD]"]

nets:
  N1: Part1.A0, Part2.AUD
  N2: Part1.D5_PWM, R1.Pin_1
  N3: Part1.D6_PWM, R2.Pin_1
  5V: Part1.5V, Part2.VCC
  N4: LED1.cathode, Part2.GND, LED2.cathode
  N5: LED1.anode, R1.Pin_0
  N6: LED2.anode, R2.Pin_0
